// Logisim project vlsi-2-test-harness-v1.circ as structural Verilog: 27 circuits, main circuit main
module main (
  input  Read_Reg_1_2,
  input  Read_Reg_1_1,
  input  Read_Reg_1_0,
  input  Write_Reg2,
  input  Write_Reg1,
  input  Write_Reg0,
  input  Read_Reg_2_2,
  input  Read_Reg_2_1,
  input  A0,
  input  Read_Reg_2_0,
  input  A1,
  input  A2,
  input  A3,
  input  op2,
  input  A4,
  input  op1,
  input  A5,
  input  op0,
  input  A6,
  input  A7,
  input  B0,
  input  B1,
  input  B2,
  input  B3,
  input  B4,
  input  B5,
  input  Regwrite,
  input  clock,
  input  B6,
  input  sel1,
  input  B7,
  input  sel0,
  output Y,
  output Y_2,
  output Y_3,
  output Y_4,
  output Y_5,
  output Y_6,
  output Y_7,
  output Y_8
);

  wire [7:0] l_8_bit_3_1_mux_bfdb9023_1_y, register_file_0e4b2f2c_1_read_data_1_494a844e,
       register_file_0e4b2f2c_1_read_data_2_24cee077;

  L_8_bit_3_1_MUX_bfdb9023 l_8_bit_3_1_mux_bfdb9023_1 (
    .A({A7, A6, A5, A4, A3, A2, A1, A0}), .B({B7, B6, B5, B4, B3, B2, B1, B0}),
    .C({Y_8, Y_7, Y_6, Y_5, Y_4, Y_3, Y_2, Y}), .sel({sel1, sel0}), .Y(l_8_bit_3_1_mux_bfdb9023_1_y));
  register_file_0e4b2f2c register_file_0e4b2f2c_1 (
    .write_register_4418c394({Write_Reg2, Write_Reg1, Write_Reg0}),
    .read_register_1_a50836c8({Read_Reg_1_2, Read_Reg_1_1, Read_Reg_1_0}),
    .read_register_2_19d239fa({Read_Reg_2_2, Read_Reg_2_1, Read_Reg_2_0}),
    .L_8_bit_input_21ceedad(l_8_bit_3_1_mux_bfdb9023_1_y), .regWrite(Regwrite), .Clock(clock),
    .read_data_1_494a844e(register_file_0e4b2f2c_1_read_data_1_494a844e),
    .read_data_2_24cee077(register_file_0e4b2f2c_1_read_data_2_24cee077));
  ALU alu_1 (
    .A(register_file_0e4b2f2c_1_read_data_1_494a844e), .B(register_file_0e4b2f2c_1_read_data_2_24cee077),
    .op({op2, op1, op0}), .D({Y_8, Y_7, Y_6, Y_5, Y_4, Y_3, Y_2, Y}));  // open: L_0V_7d9a32ef
endmodule

module register_file_0e4b2f2c (
  input  [2:0] write_register_4418c394,
  input  [2:0] read_register_1_a50836c8,
  input  [2:0] read_register_2_19d239fa,
  input  [7:0] L_8_bit_input_21ceedad,
  input  regWrite,
  input  Clock,
  output [7:0] read_data_1_494a844e,
  output [7:0] read_data_2_24cee077
);

  wire and_1_out, and_2_out, and_3_out, and_4_out, and_5_out, and_6_out, and_7_out, and_8_out,
       decoder_1_out_2, decoder_1_out_3, decoder_1_out_4, decoder_1_out_5, decoder_1_out_6, decoder_1_out_7,
       decoder_1_out_8, decoder_1_out_9;
  wire [7:0] _8_bit_register_2_out_4, _8_bit_register_3_out_4, _8_bit_register_4_out_4,
       _8_bit_register_5_out_4, _8_bit_register_6_out_4, _8_bit_register_7_out_4, _8_bit_register_8_out_4,
       _8_bit_register_out_4;

  decoder decoder_1 (
    .\input (write_register_4418c394), .out_2(decoder_1_out_2), .out_3(decoder_1_out_3),
    .out_4(decoder_1_out_4), .out_5(decoder_1_out_5), .out_6(decoder_1_out_6), .out_7(decoder_1_out_7),
    .out_8(decoder_1_out_8), .out_9(decoder_1_out_9));
  and and_1 (and_1_out, decoder_1_out_2, regWrite);
  and and_2 (and_2_out, decoder_1_out_3, regWrite);
  and and_3 (and_3_out, decoder_1_out_4, regWrite);
  and and_4 (and_4_out, decoder_1_out_5, regWrite);
  and and_5 (and_5_out, decoder_1_out_6, regWrite);
  and and_6 (and_6_out, decoder_1_out_7, regWrite);
  and and_7 (and_7_out, decoder_1_out_8, regWrite);
  and and_8 (and_8_out, decoder_1_out_9, regWrite);
  L_8_bit_register_0f6074b2 _8_bit_register (
    .\input (L_8_bit_input_21ceedad), .clock(Clock), .Reset(and_1_out), .out_4(_8_bit_register_out_4));
  L_8_bit_register_0f6074b2 _8_bit_register_2 (
    .\input (L_8_bit_input_21ceedad), .clock(Clock), .Reset(and_2_out), .out_4(_8_bit_register_2_out_4));
  L_8_bit_register_0f6074b2 _8_bit_register_3 (
    .\input (L_8_bit_input_21ceedad), .clock(Clock), .Reset(and_3_out), .out_4(_8_bit_register_3_out_4));
  L_8_bit_register_0f6074b2 _8_bit_register_4 (
    .\input (L_8_bit_input_21ceedad), .clock(Clock), .Reset(and_4_out), .out_4(_8_bit_register_4_out_4));
  L_8_bit_register_0f6074b2 _8_bit_register_5 (
    .\input (L_8_bit_input_21ceedad), .clock(Clock), .Reset(and_5_out), .out_4(_8_bit_register_5_out_4));
  L_8_bit_register_0f6074b2 _8_bit_register_6 (
    .\input (L_8_bit_input_21ceedad), .clock(Clock), .Reset(and_6_out), .out_4(_8_bit_register_6_out_4));
  L_8_bit_register_0f6074b2 _8_bit_register_7 (
    .\input (L_8_bit_input_21ceedad), .clock(Clock), .Reset(and_7_out), .out_4(_8_bit_register_7_out_4));
  L_8_bit_register_0f6074b2 _8_bit_register_8 (
    .\input (L_8_bit_input_21ceedad), .clock(Clock), .Reset(and_8_out), .out_4(_8_bit_register_8_out_4));
  L_8_bit_8_1MUX_8d78d891 l_8_bit_8_1mux_8d78d891_1 (
    .I0(_8_bit_register_out_4), .I1(_8_bit_register_2_out_4), .I2(_8_bit_register_3_out_4),
    .I3(_8_bit_register_4_out_4), .I4(_8_bit_register_5_out_4), .I5(_8_bit_register_6_out_4),
    .I6(_8_bit_register_7_out_4), .I7(_8_bit_register_8_out_4), .sel(read_register_2_19d239fa),
    .\output (read_data_2_24cee077));
  L_8_bit_8_1MUX_8d78d891 l_8_bit_8_1mux_8d78d891_2 (
    .I0(_8_bit_register_out_4), .I1(_8_bit_register_2_out_4), .I2(_8_bit_register_3_out_4),
    .I3(_8_bit_register_4_out_4), .I4(_8_bit_register_5_out_4), .I5(_8_bit_register_6_out_4),
    .I6(_8_bit_register_7_out_4), .I7(_8_bit_register_8_out_4), .sel(read_register_1_a50836c8),
    .\output (read_data_1_494a844e));
endmodule

module L_2_1_mux_e708f7bd (
  input  A,
  input  A_2,
  input  sel,
  output out_4
);

  wire and_1_out, and_2_out, not_1_out;

  not not_1 (not_1_out, sel);
  and and_1 (and_1_out, A, not_1_out);
  and and_2 (and_2_out, A_2, sel);
  or or_1 (out_4, and_1_out, and_2_out);
endmodule

// MUX
module L_8_bit_2_1_mux_aebaba51 (
  input  [7:0] A,
  input  [7:0] B,
  input  sel,
  output [7:0] \output 
);

  L_2_1_mux_e708f7bd l_2_1_mux_e708f7bd_1 (.A(A[0]), .A_2(B[0]), .sel(sel), .out_4(\output [0]));
  L_2_1_mux_e708f7bd l_2_1_mux_e708f7bd_2 (.A(A[1]), .A_2(B[1]), .sel(sel), .out_4(\output [1]));
  L_2_1_mux_e708f7bd l_2_1_mux_e708f7bd_3 (.A(A[2]), .A_2(B[2]), .sel(sel), .out_4(\output [2]));
  L_2_1_mux_e708f7bd l_2_1_mux_e708f7bd_4 (.A(A[3]), .A_2(B[3]), .sel(sel), .out_4(\output [3]));
  L_2_1_mux_e708f7bd l_2_1_mux_e708f7bd_5 (.A(A[4]), .A_2(B[4]), .sel(sel), .out_4(\output [4]));
  L_2_1_mux_e708f7bd l_2_1_mux_e708f7bd_6 (.A(A[5]), .A_2(B[5]), .sel(sel), .out_4(\output [5]));
  L_2_1_mux_e708f7bd l_2_1_mux_e708f7bd_7 (.A(A[6]), .A_2(B[6]), .sel(sel), .out_4(\output [6]));
  L_2_1_mux_e708f7bd l_2_1_mux_e708f7bd_8 (.A(A[7]), .A_2(B[7]), .sel(sel), .out_4(\output [7]));
endmodule

// MUX
module L_8_1_mux_c42f95c1 (
  input  I0,
  input  I1,
  input  I2,
  input  I3,
  input  I4,
  input  I5,
  input  I6,
  input  I7,
  input  A,
  input  B,
  input  C,
  output \output 
);

  wire and_1_out, and_2_out, and_3_out, and_4_out, and_5_out, and_6_out, and_7_out, and_8_out, not_1_out,
       not_2_out, not_3_out, or_1_out, or_2_out;

  not not_1 (not_1_out, A);
  not not_2 (not_2_out, B);
  not not_3 (not_3_out, C);
  and and_1 (and_1_out, I0, not_3_out, not_2_out, not_1_out);
  and and_2 (and_2_out, I1, C, not_2_out, not_1_out);
  and and_3 (and_3_out, I2, not_3_out, B, not_1_out);
  and and_4 (and_4_out, I3, C, B, not_1_out);
  and and_5 (and_5_out, I4, not_3_out, not_2_out, A);
  and and_6 (and_6_out, I5, C, not_2_out, A);
  and and_7 (and_7_out, I6, not_3_out, B, A);
  and and_8 (and_8_out, I7, C, B, A);
  or or_1 (or_1_out, and_1_out, and_2_out, and_3_out, and_4_out);
  or or_2 (or_2_out, and_5_out, and_6_out, and_7_out, and_8_out);
  or or_3 (\output , or_1_out, or_2_out);
endmodule

module L_8_bit_8_1MUX_8d78d891 (
  input  [7:0] I0,
  input  [7:0] I1,
  input  [7:0] I2,
  input  [7:0] I3,
  input  [7:0] I4,
  input  [7:0] I5,
  input  [7:0] I6,
  input  [7:0] I7,
  input  [2:0] sel,
  output [7:0] \output 
);

  L_8_1_mux_c42f95c1 _0 (
    .I0(I0[0]), .I1(I1[0]), .I2(I2[0]), .I3(I3[0]), .I4(I4[0]), .I5(I5[0]), .I6(I6[0]), .I7(I7[0]),
    .A(sel[2]), .B(sel[1]), .C(sel[0]), .\output (\output [0]));
  L_8_1_mux_c42f95c1 _1 (
    .I0(I0[1]), .I1(I1[1]), .I2(I2[1]), .I3(I3[1]), .I4(I4[1]), .I5(I5[1]), .I6(I6[1]), .I7(I7[1]),
    .A(sel[2]), .B(sel[1]), .C(sel[0]), .\output (\output [1]));
  L_8_1_mux_c42f95c1 _2 (
    .I0(I0[2]), .I1(I1[2]), .I2(I2[2]), .I3(I3[2]), .I4(I4[2]), .I5(I5[2]), .I6(I6[2]), .I7(I7[2]),
    .A(sel[2]), .B(sel[1]), .C(sel[0]), .\output (\output [2]));
  L_8_1_mux_c42f95c1 _3 (
    .I0(I0[3]), .I1(I1[3]), .I2(I2[3]), .I3(I3[3]), .I4(I4[3]), .I5(I5[3]), .I6(I6[3]), .I7(I7[3]),
    .A(sel[2]), .B(sel[1]), .C(sel[0]), .\output (\output [3]));
  L_8_1_mux_c42f95c1 _4 (
    .I0(I0[4]), .I1(I1[4]), .I2(I2[4]), .I3(I3[4]), .I4(I4[4]), .I5(I5[4]), .I6(I6[4]), .I7(I7[4]),
    .A(sel[2]), .B(sel[1]), .C(sel[0]), .\output (\output [4]));
  L_8_1_mux_c42f95c1 _5 (
    .I0(I0[5]), .I1(I1[5]), .I2(I2[5]), .I3(I3[5]), .I4(I4[5]), .I5(I5[5]), .I6(I6[5]), .I7(I7[5]),
    .A(sel[2]), .B(sel[1]), .C(sel[0]), .\output (\output [5]));
  L_8_1_mux_c42f95c1 _6 (
    .I0(I0[6]), .I1(I1[6]), .I2(I2[6]), .I3(I3[6]), .I4(I4[6]), .I5(I5[6]), .I6(I6[6]), .I7(I7[6]),
    .A(sel[2]), .B(sel[1]), .C(sel[0]), .\output (\output [6]));
  L_8_1_mux_c42f95c1 _7 (
    .I0(I0[7]), .I1(I1[7]), .I2(I2[7]), .I3(I3[7]), .I4(I4[7]), .I5(I5[7]), .I6(I6[7]), .I7(I7[7]),
    .A(sel[2]), .B(sel[1]), .C(sel[0]), .\output (\output [7]));
endmodule

module register (
  input  Data,
  input  Clock,
  input  Reset,
  output Q
);

  wire nand_1_out, nand_2_out, nand_3_out, nand_4_out, nand_5_out, nand_6_out, nand_8_out, not_1_out;

  not not_1 (not_1_out, Data);
  nand nand_1 (nand_1_out, Data, Clock);
  nand nand_2 (nand_2_out, not_1_out, Clock);
  nand nand_3 (nand_3_out, nand_1_out, nand_4_out);
  nand nand_4 (nand_4_out, nand_3_out, nand_2_out);
  nand nand_5 (nand_5_out, nand_3_out, Clock);
  nand nand_6 (nand_6_out, Reset, Clock);
  nand nand_7 (Q, nand_5_out, nand_8_out);
  nand nand_8 (nand_8_out, Q, nand_6_out);
endmodule

module L_8_bit_register_0f6074b2 (
  input  [7:0] \input ,
  input  clock,
  input  Reset,
  output [7:0] out_4
);

  register register_1 (.Data(\input [0]), .Clock(clock), .Reset(Reset), .Q(out_4[0]));
  register register_2 (.Data(\input [1]), .Clock(clock), .Reset(Reset), .Q(out_4[1]));
  register register_3 (.Data(\input [2]), .Clock(clock), .Reset(Reset), .Q(out_4[2]));
  register register_4 (.Data(\input [3]), .Clock(clock), .Reset(Reset), .Q(out_4[3]));
  register register_5 (.Data(\input [4]), .Clock(clock), .Reset(Reset), .Q(out_4[4]));
  register register_6 (.Data(\input [5]), .Clock(clock), .Reset(Reset), .Q(out_4[5]));
  register register_7 (.Data(\input [6]), .Clock(clock), .Reset(Reset), .Q(out_4[6]));
  register register_8 (.Data(\input [7]), .Clock(clock), .Reset(Reset), .Q(out_4[7]));
endmodule

// Decoder
module decoder (
  input  [2:0] \input ,
  output out_2,
  output out_3,
  output out_4,
  output out_5,
  output out_6,
  output out_7,
  output out_8,
  output out_9
);

  wire not_1_out, not_2_out, not_3_out;

  not not_1 (not_1_out, \input [2]);
  not not_2 (not_2_out, \input [1]);
  not not_3 (not_3_out, \input [0]);
  and and_1 (out_2, not_3_out, not_2_out, not_1_out);
  and and_2 (out_3, \input [0], not_2_out, not_1_out);
  and and_3 (out_4, not_1_out, \input [1], not_3_out);
  and and_4 (out_5, not_1_out, \input [1], \input [0]);
  and and_5 (out_6, \input [2], not_2_out, not_3_out);
  and and_6 (out_7, \input [2], not_2_out, \input [0]);
  and and_7 (out_8, \input [2], \input [1], not_3_out);
  and and_8 (out_9, \input [2], \input [1], \input [0]);
endmodule

// Full
module Adder (
  input  A,
  input  B,
  input  Cin,
  output Cout,
  output Result
);

  wire and_1_out, and_2_out, xor_1_out;

  xor xor_1 (xor_1_out, B, A);
  and and_1 (and_1_out, B, A);
  xor xor_2 (Result, Cin, xor_1_out);
  and and_2 (and_2_out, Cin, xor_1_out);
  or or_1 (Cout, and_2_out, and_1_out);
endmodule

module ALU (
  input  [2:0] op,
  input  [7:0] A,
  input  [7:0] B,
  output [7:0] L_0V_7d9a32ef,
  output [7:0] D
);

  wire [7:0] Adder_y, AND_y, Mulltiplier_p, NAND_y, NOR_y, OR_y, Subtractor_y, XOR_y;

  L_8_Bit_Adder_35c9821f Adder (.A(A), .B(B), .Y(Adder_y));
  L_8_bit_Subtractor_c11873b7 Subtractor (.A(A), .B(B), .Y(Subtractor_y));
  L_8_bit_multiplier_04def481 Mulltiplier (.A(A), .B(B), .P(Mulltiplier_p));  // open: in_1
  L_8_bit_AND_fcd1e87e AND (.A(A), .B(B), .Y(AND_y));
  L_8_bit_OR_dbfad22f OR (.A(A), .B(B), .Y(OR_y));
  L_8_bit_NAND_9d3277e4 NAND (.A(A), .B(B), .Y(NAND_y));
  L_8_bit_NOR_78e902e3 NOR (.A(A), .B(B), .Y(NOR_y));
  L_8_bit_XOR_a01a7552 XOR (.A(A), .B(B), .Y(XOR_y));
  L_8_bit_8_1MUX_8d78d891 l_8_bit_8_1mux_8d78d891_1 (
    .I0(Adder_y), .I1(Subtractor_y), .I2(Mulltiplier_p), .I3(AND_y), .I4(OR_y), .I5(NAND_y), .I6(NOR_y),
    .I7(XOR_y), .sel(op), .\output (D));
endmodule

module L_3_1_Mux_f45afe85 (
  input  A,
  input  B,
  input  C,
  input  [1:0] sel,
  output Y
);

  wire and_1_out, and_2_out, and_3_out, not_1_out, not_2_out;

  not not_1 (not_1_out, sel[1]);
  not not_2 (not_2_out, sel[0]);
  and and_1 (and_1_out, A, not_2_out, not_1_out);
  and and_2 (and_2_out, B, sel[0], not_1_out);
  and and_3 (and_3_out, C, sel[1], not_2_out);
  or or_1 (Y, and_1_out, and_2_out, and_3_out);
endmodule

// MUX
module L_8_bit_3_1_MUX_bfdb9023 (
  input  [7:0] A,
  input  [7:0] B,
  input  [7:0] C,
  input  [1:0] sel,
  output [7:0] Y
);

  L_3_1_Mux_f45afe85 l_3_1_mux_f45afe85_1 (.A(A[0]), .B(B[0]), .C(C[0]), .sel(sel), .Y(Y[0]));
  L_3_1_Mux_f45afe85 l_3_1_mux_f45afe85_2 (.A(A[1]), .B(B[1]), .C(C[1]), .sel(sel), .Y(Y[1]));
  L_3_1_Mux_f45afe85 l_3_1_mux_f45afe85_3 (.A(A[2]), .B(B[2]), .C(C[2]), .sel(sel), .Y(Y[2]));
  L_3_1_Mux_f45afe85 l_3_1_mux_f45afe85_4 (.A(A[3]), .B(B[3]), .C(C[3]), .sel(sel), .Y(Y[3]));
  L_3_1_Mux_f45afe85 l_3_1_mux_f45afe85_5 (.A(A[4]), .B(B[4]), .C(C[4]), .sel(sel), .Y(Y[4]));
  L_3_1_Mux_f45afe85 l_3_1_mux_f45afe85_6 (.A(A[5]), .B(B[5]), .C(C[5]), .sel(sel), .Y(Y[5]));
  L_3_1_Mux_f45afe85 l_3_1_mux_f45afe85_7 (.A(A[6]), .B(B[6]), .C(C[6]), .sel(sel), .Y(Y[6]));
  L_3_1_Mux_f45afe85 l_3_1_mux_f45afe85_8 (.A(A[7]), .B(B[7]), .C(C[7]), .sel(sel), .Y(Y[7]));
endmodule

module L_8_Bit_Adder_35c9821f (
  input  [7:0] A,
  input  [7:0] B,
  output [7:0] Y
);

  wire adder_2_cout, adder_3_cout, adder_4_cout, adder_5_cout, adder_6_cout, adder_7_cout,
       half_adder_1722ce90_1_cout;

  Adder adder_1 (.A(A[7]), .B(B[7]), .Cin(adder_2_cout), .Result(Y[7]));  // open: Cout
  Adder adder_2 (.A(A[6]), .B(B[6]), .Cin(adder_3_cout), .Cout(adder_2_cout), .Result(Y[6]));
  Adder adder_3 (.A(A[5]), .B(B[5]), .Cin(adder_4_cout), .Cout(adder_3_cout), .Result(Y[5]));
  Adder adder_4 (.A(A[4]), .B(B[4]), .Cin(adder_6_cout), .Cout(adder_4_cout), .Result(Y[4]));
  Adder adder_5 (.A(A[2]), .B(B[2]), .Cin(adder_7_cout), .Cout(adder_5_cout), .Result(Y[2]));
  Adder adder_6 (.A(A[3]), .B(B[3]), .Cin(adder_5_cout), .Cout(adder_6_cout), .Result(Y[3]));
  Adder adder_7 (.A(A[1]), .B(B[1]), .Cin(half_adder_1722ce90_1_cout), .Cout(adder_7_cout), .Result(Y[1]));
  Half_Adder_1722ce90 half_adder_1722ce90_1 (.A(A[0]), .B(B[0]), .Cout(half_adder_1722ce90_1_cout), .S(Y[0]));
endmodule

// Half
module Half_Adder_1722ce90 (
  input  A,
  input  B,
  output Cout,
  output S
);

  xor xor_1 (S, B, A);
  and and_1 (Cout, B, A);
endmodule

// Full
module L_1_bit_Full_Subtractor_b5bbebe8 (
  input  A,
  input  B,
  input  Bin,
  output Bout,
  output Diff
);

  wire and_1_out, and_2_out, not_1_out, not_2_out, xor_1_out;

  xor xor_1 (xor_1_out, B, Bin);
  not not_1 (not_1_out, B);
  and and_1 (and_1_out, not_1_out, Bin);
  not not_2 (not_2_out, xor_1_out);
  xor xor_2 (Diff, A, xor_1_out);
  and and_2 (and_2_out, not_2_out, A);
  or or_1 (Bout, and_2_out, and_1_out);
endmodule

// Half
module L_1_Bit_half_Subtractor_9d16e73b (
  input  A,
  input  B,
  output Bout,
  output Diff
);

  wire not_1_out;

  xor xor_1 (Diff, A, B);
  not not_1 (not_1_out, A);
  and and_1 (Bout, not_1_out, B);
endmodule

module L_8_bit_Subtractor_c11873b7 (
  input  [7:0] A,
  input  [7:0] B,
  output [7:0] Y
);

  wire l_1_bit_full_subtractor_b5bbebe8_2_bout, l_1_bit_full_subtractor_b5bbebe8_3_bout,
       l_1_bit_full_subtractor_b5bbebe8_4_bout, l_1_bit_full_subtractor_b5bbebe8_5_bout,
       l_1_bit_full_subtractor_b5bbebe8_6_bout, l_1_bit_full_subtractor_b5bbebe8_7_bout,
       l_1_bit_half_subtractor_9d16e73b_1_bout;

  L_1_bit_Full_Subtractor_b5bbebe8 l_1_bit_full_subtractor_b5bbebe8_1 (
    .A(A[7]), .B(B[7]), .Bin(l_1_bit_full_subtractor_b5bbebe8_3_bout), .Diff(Y[7]));  // open: Bout
  L_1_bit_Full_Subtractor_b5bbebe8 l_1_bit_full_subtractor_b5bbebe8_2 (
    .A(A[5]), .B(B[5]), .Bin(l_1_bit_full_subtractor_b5bbebe8_4_bout),
    .Bout(l_1_bit_full_subtractor_b5bbebe8_2_bout), .Diff(Y[5]));
  L_1_bit_Full_Subtractor_b5bbebe8 l_1_bit_full_subtractor_b5bbebe8_3 (
    .A(A[6]), .B(B[6]), .Bin(l_1_bit_full_subtractor_b5bbebe8_2_bout),
    .Bout(l_1_bit_full_subtractor_b5bbebe8_3_bout), .Diff(Y[6]));
  L_1_bit_Full_Subtractor_b5bbebe8 l_1_bit_full_subtractor_b5bbebe8_4 (
    .A(A[4]), .B(B[4]), .Bin(l_1_bit_full_subtractor_b5bbebe8_5_bout),
    .Bout(l_1_bit_full_subtractor_b5bbebe8_4_bout), .Diff(Y[4]));
  L_1_bit_Full_Subtractor_b5bbebe8 l_1_bit_full_subtractor_b5bbebe8_5 (
    .A(A[3]), .B(B[3]), .Bin(l_1_bit_full_subtractor_b5bbebe8_6_bout),
    .Bout(l_1_bit_full_subtractor_b5bbebe8_5_bout), .Diff(Y[3]));
  L_1_bit_Full_Subtractor_b5bbebe8 l_1_bit_full_subtractor_b5bbebe8_6 (
    .A(A[2]), .B(B[2]), .Bin(l_1_bit_full_subtractor_b5bbebe8_7_bout),
    .Bout(l_1_bit_full_subtractor_b5bbebe8_6_bout), .Diff(Y[2]));
  L_1_bit_Full_Subtractor_b5bbebe8 l_1_bit_full_subtractor_b5bbebe8_7 (
    .A(A[1]), .B(B[1]), .Bin(l_1_bit_half_subtractor_9d16e73b_1_bout),
    .Bout(l_1_bit_full_subtractor_b5bbebe8_7_bout), .Diff(Y[1]));
  L_1_Bit_half_Subtractor_9d16e73b l_1_bit_half_subtractor_9d16e73b_1 (
    .A(A[0]), .B(B[0]), .Bout(l_1_bit_half_subtractor_9d16e73b_1_bout), .Diff(Y[0]));
endmodule

module L_8_bit_multiplier_04def481 (
  input  in_1,
  input  [7:0] A,
  input  [7:0] B,
  output [7:0] P
);

  wire and_2_out, and_3_out, and_4_out, and_5_out, and_6_out, and_7_out, and_8_out,
       l_8_bit_adder_for_multi_b83338e0_1_cout, l_8_bit_adder_for_multi_b83338e0_1_s1,
       l_8_bit_adder_for_multi_b83338e0_1_s2, l_8_bit_adder_for_multi_b83338e0_1_s3,
       l_8_bit_adder_for_multi_b83338e0_1_s4, l_8_bit_adder_for_multi_b83338e0_1_s5,
       l_8_bit_adder_for_multi_b83338e0_1_s6, l_8_bit_adder_for_multi_b83338e0_1_s7,
       l_8_bit_adder_for_multi_b83338e0_2_cout, l_8_bit_adder_for_multi_b83338e0_2_s1,
       l_8_bit_adder_for_multi_b83338e0_2_s2, l_8_bit_adder_for_multi_b83338e0_2_s3,
       l_8_bit_adder_for_multi_b83338e0_2_s4, l_8_bit_adder_for_multi_b83338e0_2_s5,
       l_8_bit_adder_for_multi_b83338e0_2_s6, l_8_bit_adder_for_multi_b83338e0_2_s7,
       l_8_bit_adder_for_multi_b83338e0_3_cout, l_8_bit_adder_for_multi_b83338e0_3_s1,
       l_8_bit_adder_for_multi_b83338e0_3_s2, l_8_bit_adder_for_multi_b83338e0_3_s3,
       l_8_bit_adder_for_multi_b83338e0_3_s4, l_8_bit_adder_for_multi_b83338e0_3_s5,
       l_8_bit_adder_for_multi_b83338e0_3_s6, l_8_bit_adder_for_multi_b83338e0_3_s7,
       l_8_bit_adder_for_multi_b83338e0_4_cout, l_8_bit_adder_for_multi_b83338e0_4_s1,
       l_8_bit_adder_for_multi_b83338e0_4_s2, l_8_bit_adder_for_multi_b83338e0_4_s3,
       l_8_bit_adder_for_multi_b83338e0_4_s4, l_8_bit_adder_for_multi_b83338e0_4_s5,
       l_8_bit_adder_for_multi_b83338e0_4_s6, l_8_bit_adder_for_multi_b83338e0_4_s7,
       l_8_bit_adder_for_multi_b83338e0_5_cout, l_8_bit_adder_for_multi_b83338e0_5_s1,
       l_8_bit_adder_for_multi_b83338e0_5_s2, l_8_bit_adder_for_multi_b83338e0_5_s3,
       l_8_bit_adder_for_multi_b83338e0_5_s4, l_8_bit_adder_for_multi_b83338e0_5_s5,
       l_8_bit_adder_for_multi_b83338e0_5_s6, l_8_bit_adder_for_multi_b83338e0_5_s7,
       l_8_bit_adder_for_multi_b83338e0_6_cout, l_8_bit_adder_for_multi_b83338e0_6_s1,
       l_8_bit_adder_for_multi_b83338e0_6_s2, l_8_bit_adder_for_multi_b83338e0_6_s3,
       l_8_bit_adder_for_multi_b83338e0_6_s4, l_8_bit_adder_for_multi_b83338e0_6_s5,
       l_8_bit_adder_for_multi_b83338e0_6_s6, l_8_bit_adder_for_multi_b83338e0_6_s7;
  wire [7:0] and_9_out, and_17_out, and_25_out, and_33_out, and_41_out, and_49_out, and_57_out;

  and and_1 (P[0], A[0], B[0]);
  and and_2 (and_2_out, A[1], B[0]);
  and and_3 (and_3_out, A[2], B[0]);
  and and_4 (and_4_out, A[3], B[0]);
  and and_5 (and_5_out, A[4], B[0]);
  and and_6 (and_6_out, A[5], B[0]);
  and and_7 (and_7_out, A[6], B[0]);
  and and_8 (and_8_out, A[7], B[0]);
  and and_9 (and_9_out[0], A[0], B[1]);
  and and_10 (and_9_out[1], A[1], B[1]);
  and and_11 (and_9_out[2], A[2], B[1]);
  and and_12 (and_9_out[3], A[3], B[1]);
  and and_13 (and_9_out[4], A[4], B[1]);
  and and_14 (and_9_out[5], A[5], B[1]);
  and and_15 (and_9_out[6], A[6], B[1]);
  and and_16 (and_9_out[7], A[7], B[1]);
  L_8_bit_adder_for_multi_b83338e0 l_8_bit_adder_for_multi_b83338e0_1 (
    .A0(and_2_out), .A1(and_3_out), .A2(and_4_out), .A3(and_5_out), .A4(and_6_out), .A5(and_7_out),
    .A6(and_8_out), .A7(in_1), .B(and_9_out), .S0(P[1]), .S1(l_8_bit_adder_for_multi_b83338e0_1_s1),
    .S2(l_8_bit_adder_for_multi_b83338e0_1_s2), .S3(l_8_bit_adder_for_multi_b83338e0_1_s3),
    .S4(l_8_bit_adder_for_multi_b83338e0_1_s4), .S5(l_8_bit_adder_for_multi_b83338e0_1_s5),
    .S6(l_8_bit_adder_for_multi_b83338e0_1_s6), .S7(l_8_bit_adder_for_multi_b83338e0_1_s7),
    .Cout(l_8_bit_adder_for_multi_b83338e0_1_cout));
  and and_17 (and_17_out[0], A[0], B[2]);
  and and_18 (and_17_out[1], A[1], B[2]);
  and and_19 (and_17_out[2], A[2], B[2]);
  and and_20 (and_17_out[3], A[3], B[2]);
  and and_21 (and_17_out[4], A[4], B[2]);
  and and_22 (and_17_out[5], A[5], B[2]);
  and and_23 (and_17_out[6], A[6], B[2]);
  and and_24 (and_17_out[7], A[7], B[2]);
  L_8_bit_adder_for_multi_b83338e0 l_8_bit_adder_for_multi_b83338e0_2 (
    .A0(l_8_bit_adder_for_multi_b83338e0_1_s1), .A1(l_8_bit_adder_for_multi_b83338e0_1_s2),
    .A2(l_8_bit_adder_for_multi_b83338e0_1_s3), .A3(l_8_bit_adder_for_multi_b83338e0_1_s4),
    .A4(l_8_bit_adder_for_multi_b83338e0_1_s5), .A5(l_8_bit_adder_for_multi_b83338e0_1_s6),
    .A6(l_8_bit_adder_for_multi_b83338e0_1_s7), .A7(l_8_bit_adder_for_multi_b83338e0_1_cout), .B(and_17_out),
    .S0(P[2]), .S1(l_8_bit_adder_for_multi_b83338e0_2_s1), .S2(l_8_bit_adder_for_multi_b83338e0_2_s2),
    .S3(l_8_bit_adder_for_multi_b83338e0_2_s3), .S4(l_8_bit_adder_for_multi_b83338e0_2_s4),
    .S5(l_8_bit_adder_for_multi_b83338e0_2_s5), .S6(l_8_bit_adder_for_multi_b83338e0_2_s6),
    .S7(l_8_bit_adder_for_multi_b83338e0_2_s7), .Cout(l_8_bit_adder_for_multi_b83338e0_2_cout));
  and and_25 (and_25_out[0], A[0], B[3]);
  and and_26 (and_25_out[1], A[1], B[3]);
  and and_27 (and_25_out[2], A[2], B[3]);
  and and_28 (and_25_out[3], A[3], B[3]);
  and and_29 (and_25_out[4], A[4], B[3]);
  and and_30 (and_25_out[5], A[5], B[3]);
  and and_31 (and_25_out[6], A[6], B[3]);
  and and_32 (and_25_out[7], A[7], B[3]);
  L_8_bit_adder_for_multi_b83338e0 l_8_bit_adder_for_multi_b83338e0_3 (
    .A0(l_8_bit_adder_for_multi_b83338e0_2_s1), .A1(l_8_bit_adder_for_multi_b83338e0_2_s2),
    .A2(l_8_bit_adder_for_multi_b83338e0_2_s3), .A3(l_8_bit_adder_for_multi_b83338e0_2_s4),
    .A4(l_8_bit_adder_for_multi_b83338e0_2_s5), .A5(l_8_bit_adder_for_multi_b83338e0_2_s6),
    .A6(l_8_bit_adder_for_multi_b83338e0_2_s7), .A7(l_8_bit_adder_for_multi_b83338e0_2_cout), .B(and_25_out),
    .S0(P[3]), .S1(l_8_bit_adder_for_multi_b83338e0_3_s1), .S2(l_8_bit_adder_for_multi_b83338e0_3_s2),
    .S3(l_8_bit_adder_for_multi_b83338e0_3_s3), .S4(l_8_bit_adder_for_multi_b83338e0_3_s4),
    .S5(l_8_bit_adder_for_multi_b83338e0_3_s5), .S6(l_8_bit_adder_for_multi_b83338e0_3_s6),
    .S7(l_8_bit_adder_for_multi_b83338e0_3_s7), .Cout(l_8_bit_adder_for_multi_b83338e0_3_cout));
  and and_33 (and_33_out[0], A[0], B[4]);
  and and_34 (and_33_out[1], A[1], B[4]);
  and and_35 (and_33_out[2], A[2], B[4]);
  and and_36 (and_33_out[3], A[3], B[4]);
  and and_37 (and_33_out[4], A[4], B[4]);
  and and_38 (and_33_out[5], A[5], B[4]);
  and and_39 (and_33_out[6], A[6], B[4]);
  and and_40 (and_33_out[7], A[7], B[4]);
  L_8_bit_adder_for_multi_b83338e0 l_8_bit_adder_for_multi_b83338e0_4 (
    .A0(l_8_bit_adder_for_multi_b83338e0_3_s1), .A1(l_8_bit_adder_for_multi_b83338e0_3_s2),
    .A2(l_8_bit_adder_for_multi_b83338e0_3_s3), .A3(l_8_bit_adder_for_multi_b83338e0_3_s4),
    .A4(l_8_bit_adder_for_multi_b83338e0_3_s5), .A5(l_8_bit_adder_for_multi_b83338e0_3_s6),
    .A6(l_8_bit_adder_for_multi_b83338e0_3_s7), .A7(l_8_bit_adder_for_multi_b83338e0_3_cout), .B(and_33_out),
    .S0(P[4]), .S1(l_8_bit_adder_for_multi_b83338e0_4_s1), .S2(l_8_bit_adder_for_multi_b83338e0_4_s2),
    .S3(l_8_bit_adder_for_multi_b83338e0_4_s3), .S4(l_8_bit_adder_for_multi_b83338e0_4_s4),
    .S5(l_8_bit_adder_for_multi_b83338e0_4_s5), .S6(l_8_bit_adder_for_multi_b83338e0_4_s6),
    .S7(l_8_bit_adder_for_multi_b83338e0_4_s7), .Cout(l_8_bit_adder_for_multi_b83338e0_4_cout));
  and and_41 (and_41_out[0], A[0], B[5]);
  and and_42 (and_41_out[1], A[1], B[5]);
  and and_43 (and_41_out[2], A[2], B[5]);
  and and_44 (and_41_out[3], A[3], B[5]);
  and and_45 (and_41_out[4], A[4], B[5]);
  and and_46 (and_41_out[5], A[5], B[5]);
  and and_47 (and_41_out[6], A[6], B[5]);
  and and_48 (and_41_out[7], A[7], B[5]);
  L_8_bit_adder_for_multi_b83338e0 l_8_bit_adder_for_multi_b83338e0_5 (
    .A0(l_8_bit_adder_for_multi_b83338e0_4_s1), .A1(l_8_bit_adder_for_multi_b83338e0_4_s2),
    .A2(l_8_bit_adder_for_multi_b83338e0_4_s3), .A3(l_8_bit_adder_for_multi_b83338e0_4_s4),
    .A4(l_8_bit_adder_for_multi_b83338e0_4_s5), .A5(l_8_bit_adder_for_multi_b83338e0_4_s6),
    .A6(l_8_bit_adder_for_multi_b83338e0_4_s7), .A7(l_8_bit_adder_for_multi_b83338e0_4_cout), .B(and_41_out),
    .S0(P[5]), .S1(l_8_bit_adder_for_multi_b83338e0_5_s1), .S2(l_8_bit_adder_for_multi_b83338e0_5_s2),
    .S3(l_8_bit_adder_for_multi_b83338e0_5_s3), .S4(l_8_bit_adder_for_multi_b83338e0_5_s4),
    .S5(l_8_bit_adder_for_multi_b83338e0_5_s5), .S6(l_8_bit_adder_for_multi_b83338e0_5_s6),
    .S7(l_8_bit_adder_for_multi_b83338e0_5_s7), .Cout(l_8_bit_adder_for_multi_b83338e0_5_cout));
  and and_49 (and_49_out[0], A[0], B[6]);
  and and_50 (and_49_out[1], A[1], B[6]);
  and and_51 (and_49_out[2], A[2], B[6]);
  and and_52 (and_49_out[3], A[3], B[6]);
  and and_53 (and_49_out[4], A[4], B[6]);
  and and_54 (and_49_out[5], A[5], B[6]);
  and and_55 (and_49_out[6], A[6], B[6]);
  and and_56 (and_49_out[7], A[7], B[6]);
  L_8_bit_adder_for_multi_b83338e0 l_8_bit_adder_for_multi_b83338e0_6 (
    .A0(l_8_bit_adder_for_multi_b83338e0_5_s1), .A1(l_8_bit_adder_for_multi_b83338e0_5_s2),
    .A2(l_8_bit_adder_for_multi_b83338e0_5_s3), .A3(l_8_bit_adder_for_multi_b83338e0_5_s4),
    .A4(l_8_bit_adder_for_multi_b83338e0_5_s5), .A5(l_8_bit_adder_for_multi_b83338e0_5_s6),
    .A6(l_8_bit_adder_for_multi_b83338e0_5_s7), .A7(l_8_bit_adder_for_multi_b83338e0_5_cout), .B(and_49_out),
    .S0(P[6]), .S1(l_8_bit_adder_for_multi_b83338e0_6_s1), .S2(l_8_bit_adder_for_multi_b83338e0_6_s2),
    .S3(l_8_bit_adder_for_multi_b83338e0_6_s3), .S4(l_8_bit_adder_for_multi_b83338e0_6_s4),
    .S5(l_8_bit_adder_for_multi_b83338e0_6_s5), .S6(l_8_bit_adder_for_multi_b83338e0_6_s6),
    .S7(l_8_bit_adder_for_multi_b83338e0_6_s7), .Cout(l_8_bit_adder_for_multi_b83338e0_6_cout));
  and and_57 (and_57_out[0], A[0], B[7]);
  and and_58 (and_57_out[1], A[1], B[7]);
  and and_59 (and_57_out[2], A[2], B[7]);
  and and_60 (and_57_out[3], A[3], B[7]);
  and and_61 (and_57_out[4], A[4], B[7]);
  and and_62 (and_57_out[5], A[5], B[7]);
  and and_63 (and_57_out[6], A[6], B[7]);
  and and_64 (and_57_out[7], A[7], B[7]);
  L_8_bit_adder_for_multi_b83338e0 l_8_bit_adder_for_multi_b83338e0_7 (
    .A0(l_8_bit_adder_for_multi_b83338e0_6_s1), .A1(l_8_bit_adder_for_multi_b83338e0_6_s2),
    .A2(l_8_bit_adder_for_multi_b83338e0_6_s3), .A3(l_8_bit_adder_for_multi_b83338e0_6_s4),
    .A4(l_8_bit_adder_for_multi_b83338e0_6_s5), .A5(l_8_bit_adder_for_multi_b83338e0_6_s6),
    .A6(l_8_bit_adder_for_multi_b83338e0_6_s7), .A7(l_8_bit_adder_for_multi_b83338e0_6_cout), .B(and_57_out),
    .S0(P[7]));  // open: S1, S2, S3, S4, S5, S6, S7, Cout
endmodule

module L_8_bit_adder_for_multi_b83338e0 (
  input  A0,
  input  A1,
  input  A2,
  input  A3,
  input  A4,
  input  A5,
  input  A6,
  input  A7,
  input  [7:0] B,
  output S0,
  output S1,
  output S2,
  output S3,
  output S4,
  output S5,
  output S6,
  output S7,
  output Cout
);

  wire adder_2_cout, adder_3_cout, adder_4_cout, adder_5_cout, adder_6_cout, adder_7_cout,
       half_adder_1722ce90_1_cout;

  Adder adder_1 (.A(A7), .B(B[7]), .Cin(adder_2_cout), .Cout(Cout), .Result(S7));
  Adder adder_2 (.A(A6), .B(B[6]), .Cin(adder_3_cout), .Cout(adder_2_cout), .Result(S6));
  Adder adder_3 (.A(A5), .B(B[5]), .Cin(adder_4_cout), .Cout(adder_3_cout), .Result(S5));
  Adder adder_4 (.A(A4), .B(B[4]), .Cin(adder_6_cout), .Cout(adder_4_cout), .Result(S4));
  Adder adder_5 (.A(A2), .B(B[2]), .Cin(adder_7_cout), .Cout(adder_5_cout), .Result(S2));
  Adder adder_6 (.A(A3), .B(B[3]), .Cin(adder_5_cout), .Cout(adder_6_cout), .Result(S3));
  Adder adder_7 (.A(A1), .B(B[1]), .Cin(half_adder_1722ce90_1_cout), .Cout(adder_7_cout), .Result(S1));
  Half_Adder_1722ce90 half_adder_1722ce90_1 (.A(A0), .B(B[0]), .Cout(half_adder_1722ce90_1_cout), .S(S0));
endmodule

module L_8_bit_divider_3e725e82 (
  input  [7:0] A,
  input  [7:0] B,
  input  L_0_2477f575,
  output [7:0] Q
);

  wire csm_controlled_subtract_multiplex_10e31e9f_1_bout, csm_controlled_subtract_multiplex_10e31e9f_2_bout,
       csm_controlled_subtract_multiplex_10e31e9f_2_d, csm_controlled_subtract_multiplex_10e31e9f_3_bout,
       csm_controlled_subtract_multiplex_10e31e9f_4_bout, csm_controlled_subtract_multiplex_10e31e9f_4_d,
       csm_controlled_subtract_multiplex_10e31e9f_5_bout, csm_controlled_subtract_multiplex_10e31e9f_5_d,
       csm_controlled_subtract_multiplex_10e31e9f_6_bout, csm_controlled_subtract_multiplex_10e31e9f_6_d,
       csm_controlled_subtract_multiplex_10e31e9f_7_bout, csm_controlled_subtract_multiplex_10e31e9f_7_d,
       csm_controlled_subtract_multiplex_10e31e9f_8_bout, csm_controlled_subtract_multiplex_10e31e9f_8_d,
       csm_controlled_subtract_multiplex_10e31e9f_9_bout, csm_controlled_subtract_multiplex_10e31e9f_10_bout,
       csm_controlled_subtract_multiplex_10e31e9f_11_bout, csm_controlled_subtract_multiplex_10e31e9f_11_d,
       csm_controlled_subtract_multiplex_10e31e9f_12_bout, csm_controlled_subtract_multiplex_10e31e9f_12_d,
       csm_controlled_subtract_multiplex_10e31e9f_13_bout, csm_controlled_subtract_multiplex_10e31e9f_13_d,
       csm_controlled_subtract_multiplex_10e31e9f_14_bout, csm_controlled_subtract_multiplex_10e31e9f_14_d,
       csm_controlled_subtract_multiplex_10e31e9f_15_bout,
       csm_controlled_subtract_multiplex_10e31e9f_16_bout, csm_controlled_subtract_multiplex_10e31e9f_16_d,
       csm_controlled_subtract_multiplex_10e31e9f_17_bout, csm_controlled_subtract_multiplex_10e31e9f_17_d,
       csm_controlled_subtract_multiplex_10e31e9f_18_bout, csm_controlled_subtract_multiplex_10e31e9f_18_d,
       csm_controlled_subtract_multiplex_10e31e9f_19_bout, csm_controlled_subtract_multiplex_10e31e9f_19_d,
       csm_controlled_subtract_multiplex_10e31e9f_20_bout, csm_controlled_subtract_multiplex_10e31e9f_20_d,
       csm_controlled_subtract_multiplex_10e31e9f_21_bout, csm_controlled_subtract_multiplex_10e31e9f_21_d,
       csm_controlled_subtract_multiplex_10e31e9f_22_bout, csm_controlled_subtract_multiplex_10e31e9f_22_d,
       csm_controlled_subtract_multiplex_10e31e9f_23_bout, csm_controlled_subtract_multiplex_10e31e9f_23_d,
       csm_controlled_subtract_multiplex_10e31e9f_24_bout, csm_controlled_subtract_multiplex_10e31e9f_24_d,
       csm_controlled_subtract_multiplex_10e31e9f_25_bout, csm_controlled_subtract_multiplex_10e31e9f_25_d,
       csm_controlled_subtract_multiplex_10e31e9f_26_bout,
       csm_controlled_subtract_multiplex_10e31e9f_27_bout, csm_controlled_subtract_multiplex_10e31e9f_27_d,
       csm_controlled_subtract_multiplex_10e31e9f_28_bout,
       csm_controlled_subtract_multiplex_10e31e9f_29_bout, csm_controlled_subtract_multiplex_10e31e9f_29_d,
       csm_controlled_subtract_multiplex_10e31e9f_30_bout, csm_controlled_subtract_multiplex_10e31e9f_30_d,
       csm_controlled_subtract_multiplex_10e31e9f_31_bout, csm_controlled_subtract_multiplex_10e31e9f_31_d,
       csm_controlled_subtract_multiplex_10e31e9f_32_bout, csm_controlled_subtract_multiplex_10e31e9f_32_d,
       csm_controlled_subtract_multiplex_10e31e9f_33_bout, csm_controlled_subtract_multiplex_10e31e9f_33_d,
       csm_controlled_subtract_multiplex_10e31e9f_34_bout, csm_controlled_subtract_multiplex_10e31e9f_34_d,
       csm_controlled_subtract_multiplex_10e31e9f_35_bout, csm_controlled_subtract_multiplex_10e31e9f_35_d,
       csm_controlled_subtract_multiplex_10e31e9f_36_bout, csm_controlled_subtract_multiplex_10e31e9f_36_d,
       csm_controlled_subtract_multiplex_10e31e9f_37_bout, csm_controlled_subtract_multiplex_10e31e9f_37_d,
       csm_controlled_subtract_multiplex_10e31e9f_38_bout, csm_controlled_subtract_multiplex_10e31e9f_38_d,
       csm_controlled_subtract_multiplex_10e31e9f_39_bout, csm_controlled_subtract_multiplex_10e31e9f_39_d,
       csm_controlled_subtract_multiplex_10e31e9f_40_bout, csm_controlled_subtract_multiplex_10e31e9f_40_d,
       csm_controlled_subtract_multiplex_10e31e9f_41_bout, csm_controlled_subtract_multiplex_10e31e9f_41_d,
       csm_controlled_subtract_multiplex_10e31e9f_42_bout, csm_controlled_subtract_multiplex_10e31e9f_42_d,
       csm_controlled_subtract_multiplex_10e31e9f_43_bout, csm_controlled_subtract_multiplex_10e31e9f_43_d,
       csm_controlled_subtract_multiplex_10e31e9f_44_bout,
       csm_controlled_subtract_multiplex_10e31e9f_45_bout, csm_controlled_subtract_multiplex_10e31e9f_45_d,
       csm_controlled_subtract_multiplex_10e31e9f_46_bout, csm_controlled_subtract_multiplex_10e31e9f_46_d,
       csm_controlled_subtract_multiplex_10e31e9f_47_bout, csm_controlled_subtract_multiplex_10e31e9f_47_d,
       csm_controlled_subtract_multiplex_10e31e9f_48_bout, csm_controlled_subtract_multiplex_10e31e9f_48_d,
       csm_controlled_subtract_multiplex_10e31e9f_49_bout, csm_controlled_subtract_multiplex_10e31e9f_49_d,
       csm_controlled_subtract_multiplex_10e31e9f_50_bout, csm_controlled_subtract_multiplex_10e31e9f_50_d,
       csm_controlled_subtract_multiplex_10e31e9f_51_bout, csm_controlled_subtract_multiplex_10e31e9f_51_d,
       csm_controlled_subtract_multiplex_10e31e9f_52_bout, csm_controlled_subtract_multiplex_10e31e9f_52_d,
       csm_controlled_subtract_multiplex_10e31e9f_53_bout, csm_controlled_subtract_multiplex_10e31e9f_53_d,
       csm_controlled_subtract_multiplex_10e31e9f_54_bout, csm_controlled_subtract_multiplex_10e31e9f_54_d,
       csm_controlled_subtract_multiplex_10e31e9f_55_bout, csm_controlled_subtract_multiplex_10e31e9f_55_d,
       csm_controlled_subtract_multiplex_10e31e9f_56_bout, csm_controlled_subtract_multiplex_10e31e9f_56_d,
       csm_controlled_subtract_multiplex_10e31e9f_57_bout, csm_controlled_subtract_multiplex_10e31e9f_57_d,
       csm_controlled_subtract_multiplex_10e31e9f_58_bout, csm_controlled_subtract_multiplex_10e31e9f_58_d,
       csm_controlled_subtract_multiplex_10e31e9f_59_bout, csm_controlled_subtract_multiplex_10e31e9f_59_d,
       csm_controlled_subtract_multiplex_10e31e9f_60_bout, csm_controlled_subtract_multiplex_10e31e9f_60_d,
       csm_controlled_subtract_multiplex_10e31e9f_61_bout, csm_controlled_subtract_multiplex_10e31e9f_61_d,
       csm_controlled_subtract_multiplex_10e31e9f_62_bout, csm_controlled_subtract_multiplex_10e31e9f_62_d,
       csm_controlled_subtract_multiplex_10e31e9f_63_bout, csm_controlled_subtract_multiplex_10e31e9f_63_d,
       csm_controlled_subtract_multiplex_10e31e9f_64_bout, csm_controlled_subtract_multiplex_10e31e9f_64_d,
       csm_controlled_subtract_multiplex_10e31e9f_65_bout, csm_controlled_subtract_multiplex_10e31e9f_65_d,
       csm_controlled_subtract_multiplex_10e31e9f_66_bout, csm_controlled_subtract_multiplex_10e31e9f_66_d,
       csm_controlled_subtract_multiplex_10e31e9f_67_bout, csm_controlled_subtract_multiplex_10e31e9f_67_d,
       csm_controlled_subtract_multiplex_10e31e9f_68_bout, csm_controlled_subtract_multiplex_10e31e9f_68_d,
       csm_controlled_subtract_multiplex_10e31e9f_69_bout, csm_controlled_subtract_multiplex_10e31e9f_69_d,
       csm_controlled_subtract_multiplex_10e31e9f_70_bout, csm_controlled_subtract_multiplex_10e31e9f_70_d,
       csm_controlled_subtract_multiplex_10e31e9f_71_bout, csm_controlled_subtract_multiplex_10e31e9f_71_d,
       csm_controlled_subtract_multiplex_10e31e9f_72_bout, csm_controlled_subtract_multiplex_10e31e9f_72_d;

  csm_controlled_subtract_multiplex_10e31e9f csm_controlled_subtract_multiplex_10e31e9f_1 (
    .Bout(csm_controlled_subtract_multiplex_10e31e9f_1_bout),
    .os(csm_controlled_subtract_multiplex_10e31e9f_1_bout), .B(L_0_2477f575), .A(L_0_2477f575),
    .Bin(csm_controlled_subtract_multiplex_10e31e9f_2_bout));  // open: D
  not not_1 (Q[7], csm_controlled_subtract_multiplex_10e31e9f_1_bout);
  not not_2 (Q[6], csm_controlled_subtract_multiplex_10e31e9f_3_bout);
  csm_controlled_subtract_multiplex_10e31e9f csm_controlled_subtract_multiplex_10e31e9f_2 (
    .Bout(csm_controlled_subtract_multiplex_10e31e9f_2_bout), .B(B[7]), .A(A[7]),
    .D(csm_controlled_subtract_multiplex_10e31e9f_2_d),
    .Bin(csm_controlled_subtract_multiplex_10e31e9f_4_bout));  // open: os
  csm_controlled_subtract_multiplex_10e31e9f csm_controlled_subtract_multiplex_10e31e9f_3 (
    .Bout(csm_controlled_subtract_multiplex_10e31e9f_3_bout),
    .os(csm_controlled_subtract_multiplex_10e31e9f_3_bout), .B(L_0_2477f575),
    .A(csm_controlled_subtract_multiplex_10e31e9f_2_d),
    .Bin(csm_controlled_subtract_multiplex_10e31e9f_7_bout));  // open: D
  not not_3 (Q[5], csm_controlled_subtract_multiplex_10e31e9f_9_bout);
  csm_controlled_subtract_multiplex_10e31e9f csm_controlled_subtract_multiplex_10e31e9f_4 (
    .Bout(csm_controlled_subtract_multiplex_10e31e9f_4_bout), .B(B[6]), .A(A[6]),
    .D(csm_controlled_subtract_multiplex_10e31e9f_4_d),
    .Bin(csm_controlled_subtract_multiplex_10e31e9f_5_bout));  // open: os
  csm_controlled_subtract_multiplex_10e31e9f csm_controlled_subtract_multiplex_10e31e9f_5 (
    .Bout(csm_controlled_subtract_multiplex_10e31e9f_5_bout), .B(B[5]), .A(A[5]),
    .D(csm_controlled_subtract_multiplex_10e31e9f_5_d),
    .Bin(csm_controlled_subtract_multiplex_10e31e9f_11_bout));  // open: os
  csm_controlled_subtract_multiplex_10e31e9f csm_controlled_subtract_multiplex_10e31e9f_6 (
    .Bout(csm_controlled_subtract_multiplex_10e31e9f_6_bout), .B(B[6]),
    .A(csm_controlled_subtract_multiplex_10e31e9f_5_d), .D(csm_controlled_subtract_multiplex_10e31e9f_6_d),
    .Bin(csm_controlled_subtract_multiplex_10e31e9f_12_bout));  // open: os
  csm_controlled_subtract_multiplex_10e31e9f csm_controlled_subtract_multiplex_10e31e9f_7 (
    .Bout(csm_controlled_subtract_multiplex_10e31e9f_7_bout), .B(B[7]),
    .A(csm_controlled_subtract_multiplex_10e31e9f_4_d), .D(csm_controlled_subtract_multiplex_10e31e9f_7_d),
    .Bin(csm_controlled_subtract_multiplex_10e31e9f_6_bout));  // open: os
  csm_controlled_subtract_multiplex_10e31e9f csm_controlled_subtract_multiplex_10e31e9f_8 (
    .Bout(csm_controlled_subtract_multiplex_10e31e9f_8_bout), .B(B[7]),
    .A(csm_controlled_subtract_multiplex_10e31e9f_6_d), .D(csm_controlled_subtract_multiplex_10e31e9f_8_d),
    .Bin(csm_controlled_subtract_multiplex_10e31e9f_13_bout));  // open: os
  csm_controlled_subtract_multiplex_10e31e9f csm_controlled_subtract_multiplex_10e31e9f_9 (
    .Bout(csm_controlled_subtract_multiplex_10e31e9f_9_bout),
    .os(csm_controlled_subtract_multiplex_10e31e9f_9_bout), .B(L_0_2477f575),
    .A(csm_controlled_subtract_multiplex_10e31e9f_7_d),
    .Bin(csm_controlled_subtract_multiplex_10e31e9f_8_bout));  // open: D
  csm_controlled_subtract_multiplex_10e31e9f csm_controlled_subtract_multiplex_10e31e9f_10 (
    .Bout(csm_controlled_subtract_multiplex_10e31e9f_10_bout),
    .os(csm_controlled_subtract_multiplex_10e31e9f_10_bout), .B(L_0_2477f575),
    .A(csm_controlled_subtract_multiplex_10e31e9f_8_d),
    .Bin(csm_controlled_subtract_multiplex_10e31e9f_14_bout));  // open: D
  not not_4 (Q[3], csm_controlled_subtract_multiplex_10e31e9f_15_bout);
  not not_5 (Q[4], csm_controlled_subtract_multiplex_10e31e9f_10_bout);
  csm_controlled_subtract_multiplex_10e31e9f csm_controlled_subtract_multiplex_10e31e9f_11 (
    .Bout(csm_controlled_subtract_multiplex_10e31e9f_11_bout), .B(B[4]), .A(A[4]),
    .D(csm_controlled_subtract_multiplex_10e31e9f_11_d),
    .Bin(csm_controlled_subtract_multiplex_10e31e9f_16_bout));  // open: os
  csm_controlled_subtract_multiplex_10e31e9f csm_controlled_subtract_multiplex_10e31e9f_12 (
    .Bout(csm_controlled_subtract_multiplex_10e31e9f_12_bout), .B(B[5]),
    .A(csm_controlled_subtract_multiplex_10e31e9f_11_d), .D(csm_controlled_subtract_multiplex_10e31e9f_12_d),
    .Bin(csm_controlled_subtract_multiplex_10e31e9f_19_bout));  // open: os
  csm_controlled_subtract_multiplex_10e31e9f csm_controlled_subtract_multiplex_10e31e9f_13 (
    .Bout(csm_controlled_subtract_multiplex_10e31e9f_13_bout), .B(B[6]),
    .A(csm_controlled_subtract_multiplex_10e31e9f_12_d), .D(csm_controlled_subtract_multiplex_10e31e9f_13_d),
    .Bin(csm_controlled_subtract_multiplex_10e31e9f_21_bout));  // open: os
  csm_controlled_subtract_multiplex_10e31e9f csm_controlled_subtract_multiplex_10e31e9f_14 (
    .Bout(csm_controlled_subtract_multiplex_10e31e9f_14_bout), .B(B[7]),
    .A(csm_controlled_subtract_multiplex_10e31e9f_13_d), .D(csm_controlled_subtract_multiplex_10e31e9f_14_d),
    .Bin(csm_controlled_subtract_multiplex_10e31e9f_22_bout));  // open: os
  csm_controlled_subtract_multiplex_10e31e9f csm_controlled_subtract_multiplex_10e31e9f_15 (
    .Bout(csm_controlled_subtract_multiplex_10e31e9f_15_bout),
    .os(csm_controlled_subtract_multiplex_10e31e9f_15_bout), .B(L_0_2477f575),
    .A(csm_controlled_subtract_multiplex_10e31e9f_14_d),
    .Bin(csm_controlled_subtract_multiplex_10e31e9f_25_bout));  // open: D
  not not_6 (Q[2], csm_controlled_subtract_multiplex_10e31e9f_26_bout);
  csm_controlled_subtract_multiplex_10e31e9f csm_controlled_subtract_multiplex_10e31e9f_16 (
    .Bout(csm_controlled_subtract_multiplex_10e31e9f_16_bout), .B(B[3]), .A(A[3]),
    .D(csm_controlled_subtract_multiplex_10e31e9f_16_d),
    .Bin(csm_controlled_subtract_multiplex_10e31e9f_17_bout));  // open: os
  csm_controlled_subtract_multiplex_10e31e9f csm_controlled_subtract_multiplex_10e31e9f_17 (
    .Bout(csm_controlled_subtract_multiplex_10e31e9f_17_bout), .B(B[2]), .A(A[2]),
    .D(csm_controlled_subtract_multiplex_10e31e9f_17_d),
    .Bin(csm_controlled_subtract_multiplex_10e31e9f_29_bout));  // open: os
  csm_controlled_subtract_multiplex_10e31e9f csm_controlled_subtract_multiplex_10e31e9f_18 (
    .Bout(csm_controlled_subtract_multiplex_10e31e9f_18_bout), .B(B[3]),
    .A(csm_controlled_subtract_multiplex_10e31e9f_17_d), .D(csm_controlled_subtract_multiplex_10e31e9f_18_d),
    .Bin(csm_controlled_subtract_multiplex_10e31e9f_32_bout));  // open: os
  csm_controlled_subtract_multiplex_10e31e9f csm_controlled_subtract_multiplex_10e31e9f_19 (
    .Bout(csm_controlled_subtract_multiplex_10e31e9f_19_bout), .B(B[4]),
    .A(csm_controlled_subtract_multiplex_10e31e9f_16_d), .D(csm_controlled_subtract_multiplex_10e31e9f_19_d),
    .Bin(csm_controlled_subtract_multiplex_10e31e9f_18_bout));  // open: os
  csm_controlled_subtract_multiplex_10e31e9f csm_controlled_subtract_multiplex_10e31e9f_20 (
    .Bout(csm_controlled_subtract_multiplex_10e31e9f_20_bout), .B(B[4]),
    .A(csm_controlled_subtract_multiplex_10e31e9f_18_d), .D(csm_controlled_subtract_multiplex_10e31e9f_20_d),
    .Bin(csm_controlled_subtract_multiplex_10e31e9f_34_bout));  // open: os
  csm_controlled_subtract_multiplex_10e31e9f csm_controlled_subtract_multiplex_10e31e9f_21 (
    .Bout(csm_controlled_subtract_multiplex_10e31e9f_21_bout), .B(B[5]),
    .A(csm_controlled_subtract_multiplex_10e31e9f_19_d), .D(csm_controlled_subtract_multiplex_10e31e9f_21_d),
    .Bin(csm_controlled_subtract_multiplex_10e31e9f_20_bout));  // open: os
  csm_controlled_subtract_multiplex_10e31e9f csm_controlled_subtract_multiplex_10e31e9f_22 (
    .Bout(csm_controlled_subtract_multiplex_10e31e9f_22_bout), .B(B[6]),
    .A(csm_controlled_subtract_multiplex_10e31e9f_21_d), .D(csm_controlled_subtract_multiplex_10e31e9f_22_d),
    .Bin(csm_controlled_subtract_multiplex_10e31e9f_23_bout));  // open: os
  csm_controlled_subtract_multiplex_10e31e9f csm_controlled_subtract_multiplex_10e31e9f_23 (
    .Bout(csm_controlled_subtract_multiplex_10e31e9f_23_bout), .B(B[5]),
    .A(csm_controlled_subtract_multiplex_10e31e9f_20_d), .D(csm_controlled_subtract_multiplex_10e31e9f_23_d),
    .Bin(csm_controlled_subtract_multiplex_10e31e9f_35_bout));  // open: os
  csm_controlled_subtract_multiplex_10e31e9f csm_controlled_subtract_multiplex_10e31e9f_24 (
    .Bout(csm_controlled_subtract_multiplex_10e31e9f_24_bout), .B(B[6]),
    .A(csm_controlled_subtract_multiplex_10e31e9f_23_d), .D(csm_controlled_subtract_multiplex_10e31e9f_24_d),
    .Bin(csm_controlled_subtract_multiplex_10e31e9f_37_bout));  // open: os
  csm_controlled_subtract_multiplex_10e31e9f csm_controlled_subtract_multiplex_10e31e9f_25 (
    .Bout(csm_controlled_subtract_multiplex_10e31e9f_25_bout), .B(B[7]),
    .A(csm_controlled_subtract_multiplex_10e31e9f_22_d), .D(csm_controlled_subtract_multiplex_10e31e9f_25_d),
    .Bin(csm_controlled_subtract_multiplex_10e31e9f_24_bout));  // open: os
  csm_controlled_subtract_multiplex_10e31e9f csm_controlled_subtract_multiplex_10e31e9f_26 (
    .Bout(csm_controlled_subtract_multiplex_10e31e9f_26_bout),
    .os(csm_controlled_subtract_multiplex_10e31e9f_26_bout), .B(L_0_2477f575),
    .A(csm_controlled_subtract_multiplex_10e31e9f_25_d),
    .Bin(csm_controlled_subtract_multiplex_10e31e9f_27_bout));  // open: D
  csm_controlled_subtract_multiplex_10e31e9f csm_controlled_subtract_multiplex_10e31e9f_27 (
    .Bout(csm_controlled_subtract_multiplex_10e31e9f_27_bout), .B(B[7]),
    .A(csm_controlled_subtract_multiplex_10e31e9f_24_d), .D(csm_controlled_subtract_multiplex_10e31e9f_27_d),
    .Bin(csm_controlled_subtract_multiplex_10e31e9f_39_bout));  // open: os
  csm_controlled_subtract_multiplex_10e31e9f csm_controlled_subtract_multiplex_10e31e9f_28 (
    .Bout(csm_controlled_subtract_multiplex_10e31e9f_28_bout),
    .os(csm_controlled_subtract_multiplex_10e31e9f_28_bout), .B(L_0_2477f575),
    .A(csm_controlled_subtract_multiplex_10e31e9f_27_d),
    .Bin(csm_controlled_subtract_multiplex_10e31e9f_41_bout));  // open: D
  not not_7 (Q[0], csm_controlled_subtract_multiplex_10e31e9f_44_bout);
  not not_8 (Q[1], csm_controlled_subtract_multiplex_10e31e9f_28_bout);
  csm_controlled_subtract_multiplex_10e31e9f csm_controlled_subtract_multiplex_10e31e9f_29 (
    .Bout(csm_controlled_subtract_multiplex_10e31e9f_29_bout), .B(B[1]), .A(A[1]),
    .D(csm_controlled_subtract_multiplex_10e31e9f_29_d),
    .Bin(csm_controlled_subtract_multiplex_10e31e9f_30_bout));  // open: os
  csm_controlled_subtract_multiplex_10e31e9f csm_controlled_subtract_multiplex_10e31e9f_30 (
    .Bout(csm_controlled_subtract_multiplex_10e31e9f_30_bout), .B(B[0]), .A(A[0]),
    .D(csm_controlled_subtract_multiplex_10e31e9f_30_d));  // open: os, Bin
  csm_controlled_subtract_multiplex_10e31e9f csm_controlled_subtract_multiplex_10e31e9f_31 (
    .Bout(csm_controlled_subtract_multiplex_10e31e9f_31_bout), .B(B[1]),
    .A(csm_controlled_subtract_multiplex_10e31e9f_30_d), .D(csm_controlled_subtract_multiplex_10e31e9f_31_d),
    .Bin(csm_controlled_subtract_multiplex_10e31e9f_45_bout));  // open: os
  csm_controlled_subtract_multiplex_10e31e9f csm_controlled_subtract_multiplex_10e31e9f_32 (
    .Bout(csm_controlled_subtract_multiplex_10e31e9f_32_bout), .B(B[2]),
    .A(csm_controlled_subtract_multiplex_10e31e9f_29_d), .D(csm_controlled_subtract_multiplex_10e31e9f_32_d),
    .Bin(csm_controlled_subtract_multiplex_10e31e9f_31_bout));  // open: os
  csm_controlled_subtract_multiplex_10e31e9f csm_controlled_subtract_multiplex_10e31e9f_33 (
    .Bout(csm_controlled_subtract_multiplex_10e31e9f_33_bout), .B(B[2]),
    .A(csm_controlled_subtract_multiplex_10e31e9f_31_d), .D(csm_controlled_subtract_multiplex_10e31e9f_33_d),
    .Bin(csm_controlled_subtract_multiplex_10e31e9f_46_bout));  // open: os
  csm_controlled_subtract_multiplex_10e31e9f csm_controlled_subtract_multiplex_10e31e9f_34 (
    .Bout(csm_controlled_subtract_multiplex_10e31e9f_34_bout), .B(B[3]),
    .A(csm_controlled_subtract_multiplex_10e31e9f_32_d), .D(csm_controlled_subtract_multiplex_10e31e9f_34_d),
    .Bin(csm_controlled_subtract_multiplex_10e31e9f_33_bout));  // open: os
  csm_controlled_subtract_multiplex_10e31e9f csm_controlled_subtract_multiplex_10e31e9f_35 (
    .Bout(csm_controlled_subtract_multiplex_10e31e9f_35_bout), .B(B[4]),
    .A(csm_controlled_subtract_multiplex_10e31e9f_34_d), .D(csm_controlled_subtract_multiplex_10e31e9f_35_d),
    .Bin(csm_controlled_subtract_multiplex_10e31e9f_36_bout));  // open: os
  csm_controlled_subtract_multiplex_10e31e9f csm_controlled_subtract_multiplex_10e31e9f_36 (
    .Bout(csm_controlled_subtract_multiplex_10e31e9f_36_bout), .B(B[3]),
    .A(csm_controlled_subtract_multiplex_10e31e9f_33_d), .D(csm_controlled_subtract_multiplex_10e31e9f_36_d),
    .Bin(csm_controlled_subtract_multiplex_10e31e9f_47_bout));  // open: os
  csm_controlled_subtract_multiplex_10e31e9f csm_controlled_subtract_multiplex_10e31e9f_37 (
    .Bout(csm_controlled_subtract_multiplex_10e31e9f_37_bout), .B(B[5]),
    .A(csm_controlled_subtract_multiplex_10e31e9f_35_d), .D(csm_controlled_subtract_multiplex_10e31e9f_37_d),
    .Bin(csm_controlled_subtract_multiplex_10e31e9f_38_bout));  // open: os
  csm_controlled_subtract_multiplex_10e31e9f csm_controlled_subtract_multiplex_10e31e9f_38 (
    .Bout(csm_controlled_subtract_multiplex_10e31e9f_38_bout), .B(B[4]),
    .A(csm_controlled_subtract_multiplex_10e31e9f_36_d), .D(csm_controlled_subtract_multiplex_10e31e9f_38_d),
    .Bin(csm_controlled_subtract_multiplex_10e31e9f_48_bout));  // open: os
  csm_controlled_subtract_multiplex_10e31e9f csm_controlled_subtract_multiplex_10e31e9f_39 (
    .Bout(csm_controlled_subtract_multiplex_10e31e9f_39_bout), .B(B[6]),
    .A(csm_controlled_subtract_multiplex_10e31e9f_37_d), .D(csm_controlled_subtract_multiplex_10e31e9f_39_d),
    .Bin(csm_controlled_subtract_multiplex_10e31e9f_40_bout));  // open: os
  csm_controlled_subtract_multiplex_10e31e9f csm_controlled_subtract_multiplex_10e31e9f_40 (
    .Bout(csm_controlled_subtract_multiplex_10e31e9f_40_bout), .B(B[5]),
    .A(csm_controlled_subtract_multiplex_10e31e9f_38_d), .D(csm_controlled_subtract_multiplex_10e31e9f_40_d),
    .Bin(csm_controlled_subtract_multiplex_10e31e9f_49_bout));  // open: os
  csm_controlled_subtract_multiplex_10e31e9f csm_controlled_subtract_multiplex_10e31e9f_41 (
    .Bout(csm_controlled_subtract_multiplex_10e31e9f_41_bout), .B(B[7]),
    .A(csm_controlled_subtract_multiplex_10e31e9f_39_d), .D(csm_controlled_subtract_multiplex_10e31e9f_41_d),
    .Bin(csm_controlled_subtract_multiplex_10e31e9f_42_bout));  // open: os
  csm_controlled_subtract_multiplex_10e31e9f csm_controlled_subtract_multiplex_10e31e9f_42 (
    .Bout(csm_controlled_subtract_multiplex_10e31e9f_42_bout), .B(B[6]),
    .A(csm_controlled_subtract_multiplex_10e31e9f_40_d), .D(csm_controlled_subtract_multiplex_10e31e9f_42_d),
    .Bin(csm_controlled_subtract_multiplex_10e31e9f_50_bout));  // open: os
  csm_controlled_subtract_multiplex_10e31e9f csm_controlled_subtract_multiplex_10e31e9f_43 (
    .Bout(csm_controlled_subtract_multiplex_10e31e9f_43_bout), .B(B[7]),
    .A(csm_controlled_subtract_multiplex_10e31e9f_42_d), .D(csm_controlled_subtract_multiplex_10e31e9f_43_d),
    .Bin(csm_controlled_subtract_multiplex_10e31e9f_51_bout));  // open: os
  csm_controlled_subtract_multiplex_10e31e9f csm_controlled_subtract_multiplex_10e31e9f_44 (
    .Bout(csm_controlled_subtract_multiplex_10e31e9f_44_bout),
    .os(csm_controlled_subtract_multiplex_10e31e9f_44_bout), .B(L_0_2477f575),
    .A(csm_controlled_subtract_multiplex_10e31e9f_41_d),
    .Bin(csm_controlled_subtract_multiplex_10e31e9f_43_bout));  // open: D
  csm_controlled_subtract_multiplex_10e31e9f csm_controlled_subtract_multiplex_10e31e9f_45 (
    .Bout(csm_controlled_subtract_multiplex_10e31e9f_45_bout), .B(B[0]), .A(A[7]),
    .D(csm_controlled_subtract_multiplex_10e31e9f_45_d));  // open: os, Bin
  csm_controlled_subtract_multiplex_10e31e9f csm_controlled_subtract_multiplex_10e31e9f_46 (
    .Bout(csm_controlled_subtract_multiplex_10e31e9f_46_bout), .B(B[1]),
    .A(csm_controlled_subtract_multiplex_10e31e9f_45_d), .D(csm_controlled_subtract_multiplex_10e31e9f_46_d),
    .Bin(csm_controlled_subtract_multiplex_10e31e9f_52_bout));  // open: os
  csm_controlled_subtract_multiplex_10e31e9f csm_controlled_subtract_multiplex_10e31e9f_47 (
    .Bout(csm_controlled_subtract_multiplex_10e31e9f_47_bout), .B(B[2]),
    .A(csm_controlled_subtract_multiplex_10e31e9f_46_d), .D(csm_controlled_subtract_multiplex_10e31e9f_47_d),
    .Bin(csm_controlled_subtract_multiplex_10e31e9f_54_bout));  // open: os
  csm_controlled_subtract_multiplex_10e31e9f csm_controlled_subtract_multiplex_10e31e9f_48 (
    .Bout(csm_controlled_subtract_multiplex_10e31e9f_48_bout), .B(B[3]),
    .A(csm_controlled_subtract_multiplex_10e31e9f_47_d), .D(csm_controlled_subtract_multiplex_10e31e9f_48_d),
    .Bin(csm_controlled_subtract_multiplex_10e31e9f_56_bout));  // open: os
  csm_controlled_subtract_multiplex_10e31e9f csm_controlled_subtract_multiplex_10e31e9f_49 (
    .Bout(csm_controlled_subtract_multiplex_10e31e9f_49_bout), .B(B[4]),
    .A(csm_controlled_subtract_multiplex_10e31e9f_48_d), .D(csm_controlled_subtract_multiplex_10e31e9f_49_d),
    .Bin(csm_controlled_subtract_multiplex_10e31e9f_58_bout));  // open: os
  csm_controlled_subtract_multiplex_10e31e9f csm_controlled_subtract_multiplex_10e31e9f_50 (
    .Bout(csm_controlled_subtract_multiplex_10e31e9f_50_bout), .B(B[5]),
    .A(csm_controlled_subtract_multiplex_10e31e9f_49_d), .D(csm_controlled_subtract_multiplex_10e31e9f_50_d),
    .Bin(csm_controlled_subtract_multiplex_10e31e9f_60_bout));  // open: os
  csm_controlled_subtract_multiplex_10e31e9f csm_controlled_subtract_multiplex_10e31e9f_51 (
    .Bout(csm_controlled_subtract_multiplex_10e31e9f_51_bout), .B(B[6]),
    .A(csm_controlled_subtract_multiplex_10e31e9f_50_d), .D(csm_controlled_subtract_multiplex_10e31e9f_51_d),
    .Bin(csm_controlled_subtract_multiplex_10e31e9f_62_bout));  // open: os
  csm_controlled_subtract_multiplex_10e31e9f csm_controlled_subtract_multiplex_10e31e9f_52 (
    .Bout(csm_controlled_subtract_multiplex_10e31e9f_52_bout), .B(B[0]), .A(A[6]),
    .D(csm_controlled_subtract_multiplex_10e31e9f_52_d));  // open: os, Bin
  csm_controlled_subtract_multiplex_10e31e9f csm_controlled_subtract_multiplex_10e31e9f_53 (
    .Bout(csm_controlled_subtract_multiplex_10e31e9f_53_bout), .B(B[0]), .A(A[5]),
    .D(csm_controlled_subtract_multiplex_10e31e9f_53_d));  // open: os, Bin
  csm_controlled_subtract_multiplex_10e31e9f csm_controlled_subtract_multiplex_10e31e9f_54 (
    .Bout(csm_controlled_subtract_multiplex_10e31e9f_54_bout), .B(B[1]),
    .A(csm_controlled_subtract_multiplex_10e31e9f_52_d), .D(csm_controlled_subtract_multiplex_10e31e9f_54_d),
    .Bin(csm_controlled_subtract_multiplex_10e31e9f_53_bout));  // open: os
  csm_controlled_subtract_multiplex_10e31e9f csm_controlled_subtract_multiplex_10e31e9f_55 (
    .Bout(csm_controlled_subtract_multiplex_10e31e9f_55_bout), .B(B[1]),
    .A(csm_controlled_subtract_multiplex_10e31e9f_53_d), .D(csm_controlled_subtract_multiplex_10e31e9f_55_d),
    .Bin(csm_controlled_subtract_multiplex_10e31e9f_63_bout));  // open: os
  csm_controlled_subtract_multiplex_10e31e9f csm_controlled_subtract_multiplex_10e31e9f_56 (
    .Bout(csm_controlled_subtract_multiplex_10e31e9f_56_bout), .B(B[2]),
    .A(csm_controlled_subtract_multiplex_10e31e9f_54_d), .D(csm_controlled_subtract_multiplex_10e31e9f_56_d),
    .Bin(csm_controlled_subtract_multiplex_10e31e9f_55_bout));  // open: os
  csm_controlled_subtract_multiplex_10e31e9f csm_controlled_subtract_multiplex_10e31e9f_57 (
    .Bout(csm_controlled_subtract_multiplex_10e31e9f_57_bout), .B(B[2]),
    .A(csm_controlled_subtract_multiplex_10e31e9f_55_d), .D(csm_controlled_subtract_multiplex_10e31e9f_57_d),
    .Bin(csm_controlled_subtract_multiplex_10e31e9f_64_bout));  // open: os
  csm_controlled_subtract_multiplex_10e31e9f csm_controlled_subtract_multiplex_10e31e9f_58 (
    .Bout(csm_controlled_subtract_multiplex_10e31e9f_58_bout), .B(B[3]),
    .A(csm_controlled_subtract_multiplex_10e31e9f_56_d), .D(csm_controlled_subtract_multiplex_10e31e9f_58_d),
    .Bin(csm_controlled_subtract_multiplex_10e31e9f_57_bout));  // open: os
  csm_controlled_subtract_multiplex_10e31e9f csm_controlled_subtract_multiplex_10e31e9f_59 (
    .Bout(csm_controlled_subtract_multiplex_10e31e9f_59_bout), .B(B[3]),
    .A(csm_controlled_subtract_multiplex_10e31e9f_57_d), .D(csm_controlled_subtract_multiplex_10e31e9f_59_d),
    .Bin(csm_controlled_subtract_multiplex_10e31e9f_65_bout));  // open: os
  csm_controlled_subtract_multiplex_10e31e9f csm_controlled_subtract_multiplex_10e31e9f_60 (
    .Bout(csm_controlled_subtract_multiplex_10e31e9f_60_bout), .B(B[4]),
    .A(csm_controlled_subtract_multiplex_10e31e9f_58_d), .D(csm_controlled_subtract_multiplex_10e31e9f_60_d),
    .Bin(csm_controlled_subtract_multiplex_10e31e9f_59_bout));  // open: os
  csm_controlled_subtract_multiplex_10e31e9f csm_controlled_subtract_multiplex_10e31e9f_61 (
    .Bout(csm_controlled_subtract_multiplex_10e31e9f_61_bout), .B(B[4]),
    .A(csm_controlled_subtract_multiplex_10e31e9f_59_d), .D(csm_controlled_subtract_multiplex_10e31e9f_61_d),
    .Bin(csm_controlled_subtract_multiplex_10e31e9f_66_bout));  // open: os
  csm_controlled_subtract_multiplex_10e31e9f csm_controlled_subtract_multiplex_10e31e9f_62 (
    .Bout(csm_controlled_subtract_multiplex_10e31e9f_62_bout), .B(B[5]),
    .A(csm_controlled_subtract_multiplex_10e31e9f_60_d), .D(csm_controlled_subtract_multiplex_10e31e9f_62_d),
    .Bin(csm_controlled_subtract_multiplex_10e31e9f_61_bout));  // open: os
  csm_controlled_subtract_multiplex_10e31e9f csm_controlled_subtract_multiplex_10e31e9f_63 (
    .Bout(csm_controlled_subtract_multiplex_10e31e9f_63_bout), .B(B[0]), .A(A[4]),
    .D(csm_controlled_subtract_multiplex_10e31e9f_63_d));  // open: os, Bin
  csm_controlled_subtract_multiplex_10e31e9f csm_controlled_subtract_multiplex_10e31e9f_64 (
    .Bout(csm_controlled_subtract_multiplex_10e31e9f_64_bout), .B(B[1]),
    .A(csm_controlled_subtract_multiplex_10e31e9f_63_d), .D(csm_controlled_subtract_multiplex_10e31e9f_64_d),
    .Bin(csm_controlled_subtract_multiplex_10e31e9f_67_bout));  // open: os
  csm_controlled_subtract_multiplex_10e31e9f csm_controlled_subtract_multiplex_10e31e9f_65 (
    .Bout(csm_controlled_subtract_multiplex_10e31e9f_65_bout), .B(B[2]),
    .A(csm_controlled_subtract_multiplex_10e31e9f_64_d), .D(csm_controlled_subtract_multiplex_10e31e9f_65_d),
    .Bin(csm_controlled_subtract_multiplex_10e31e9f_68_bout));  // open: os
  csm_controlled_subtract_multiplex_10e31e9f csm_controlled_subtract_multiplex_10e31e9f_66 (
    .Bout(csm_controlled_subtract_multiplex_10e31e9f_66_bout), .B(B[3]),
    .A(csm_controlled_subtract_multiplex_10e31e9f_65_d), .D(csm_controlled_subtract_multiplex_10e31e9f_66_d),
    .Bin(csm_controlled_subtract_multiplex_10e31e9f_71_bout));  // open: os
  csm_controlled_subtract_multiplex_10e31e9f csm_controlled_subtract_multiplex_10e31e9f_67 (
    .Bout(csm_controlled_subtract_multiplex_10e31e9f_67_bout), .B(B[0]), .A(A[3]),
    .D(csm_controlled_subtract_multiplex_10e31e9f_67_d));  // open: os, Bin
  csm_controlled_subtract_multiplex_10e31e9f csm_controlled_subtract_multiplex_10e31e9f_68 (
    .Bout(csm_controlled_subtract_multiplex_10e31e9f_68_bout), .B(B[1]),
    .A(csm_controlled_subtract_multiplex_10e31e9f_67_d), .D(csm_controlled_subtract_multiplex_10e31e9f_68_d),
    .Bin(csm_controlled_subtract_multiplex_10e31e9f_69_bout));  // open: os
  csm_controlled_subtract_multiplex_10e31e9f csm_controlled_subtract_multiplex_10e31e9f_69 (
    .Bout(csm_controlled_subtract_multiplex_10e31e9f_69_bout), .B(B[0]), .A(A[2]),
    .D(csm_controlled_subtract_multiplex_10e31e9f_69_d));  // open: os, Bin
  csm_controlled_subtract_multiplex_10e31e9f csm_controlled_subtract_multiplex_10e31e9f_70 (
    .Bout(csm_controlled_subtract_multiplex_10e31e9f_70_bout), .B(B[1]),
    .A(csm_controlled_subtract_multiplex_10e31e9f_69_d), .D(csm_controlled_subtract_multiplex_10e31e9f_70_d),
    .Bin(csm_controlled_subtract_multiplex_10e31e9f_72_bout));  // open: os
  csm_controlled_subtract_multiplex_10e31e9f csm_controlled_subtract_multiplex_10e31e9f_71 (
    .Bout(csm_controlled_subtract_multiplex_10e31e9f_71_bout), .B(B[2]),
    .A(csm_controlled_subtract_multiplex_10e31e9f_68_d), .D(csm_controlled_subtract_multiplex_10e31e9f_71_d),
    .Bin(csm_controlled_subtract_multiplex_10e31e9f_70_bout));  // open: os
  csm_controlled_subtract_multiplex_10e31e9f csm_controlled_subtract_multiplex_10e31e9f_72 (
    .Bout(csm_controlled_subtract_multiplex_10e31e9f_72_bout), .B(B[0]), .A(A[1]),
    .D(csm_controlled_subtract_multiplex_10e31e9f_72_d));  // open: os, Bin
endmodule

module csm_controlled_subtract_multiplex_10e31e9f (
  input  B,
  input  A,
  input  Bin,
  input  os,
  output Bout,
  output D
);

  wire and_1_out, and_2_out, l_1_bit_full_subtractor_b5bbebe8_1_diff, not_1_out;

  L_1_bit_Full_Subtractor_b5bbebe8 l_1_bit_full_subtractor_b5bbebe8_1 (
    .A(A), .B(B), .Bin(Bin), .Bout(Bout), .Diff(l_1_bit_full_subtractor_b5bbebe8_1_diff));
  and and_1 (and_1_out, l_1_bit_full_subtractor_b5bbebe8_1_diff, not_1_out);
  not not_1 (not_1_out, os);
  and and_2 (and_2_out, A, os);
  or or_1 (D, and_1_out, and_2_out);
endmodule

module L_8_bit_AND_fcd1e87e (
  input  [7:0] A,
  input  [7:0] B,
  output [7:0] Y
);

  assign Y = A & B;  // AND_Gate and_1, 8 bits wide
endmodule

module L_8_bit_OR_dbfad22f (
  input  [7:0] A,
  input  [7:0] B,
  output [7:0] Y
);

  assign Y = A | B;  // OR_Gate or_1, 8 bits wide
endmodule

module L_8_bit_NAND_9d3277e4 (
  input  [7:0] A,
  input  [7:0] B,
  output [7:0] Y
);

  assign Y = ~(A & B);  // NAND_Gate nand_1, 8 bits wide
endmodule

module L_8_bit_NOR_78e902e3 (
  input  [7:0] A,
  input  [7:0] B,
  output [7:0] Y
);

  assign Y = ~(A | B);  // NOR_Gate nor_1, 8 bits wide
endmodule

module L_8_bit_XOR_a01a7552 (
  input  [7:0] A,
  input  [7:0] B,
  output [7:0] Y
);

  assign Y = A ^ B;  // XOR_Gate xor_1, 8 bits wide
endmodule
